// Logisim project team.circ as structural Verilog: 1 circuit, main circuit main
module main (
  input  F1_INPUT,
  input  F0_INPUT,
  input  [1:0] in_3,
  input  [3:0] in_4,
  input  [1:0] in_5,
  input  [3:0] in_6,
  output STATE,
  output STATE_2,
  output NEXT,
  output NEXT_2
);

  wire and_1_out, and_2_out, and_3_out, and_4_out, and_5_out, and_6_out, CLK_out, comparator_1_eq,
       comparator_1_gt, comparator_1_lt, comparator_2_eq, comparator_2_gt, comparator_2_lt, comparator_3_eq,
       comparator_3_lt, comparator_4_eq, comparator_4_gt, comparator_5_eq, comparator_5_gt, comparator_6_eq,
       comparator_6_lt, not_1_out, xnor_1_out, xor_1_out;
  wire [3:0] adder_1_out, adder_2_out, adder_3_out, subtractor_1_out, subtractor_2_out, subtractor_3_out;

  not not_1 (not_1_out, STATE_2);
  and and_1 (and_1_out, STATE, STATE_2);
  and and_2 (and_2_out, STATE_2, F1_INPUT);
  and and_3 (and_3_out, F0_INPUT, not_1_out);
  xnor xnor_1 (xnor_1_out, STATE, F1_INPUT);
  xor xor_1 (xor_1_out, STATE, F1_INPUT);
  and and_4 (and_4_out, STATE, F1_INPUT);
  and and_5 (and_5_out, F0_INPUT, xnor_1_out);
  and and_6 (and_6_out, not_1_out, xor_1_out);
  or or_1 (NEXT, and_1_out, and_4_out, and_2_out);
  or or_2 (NEXT_2, and_3_out, and_5_out, and_6_out);
  D_Flip_Flop #(.trigger("falling")) Q1 (.clk(CLK_out), .D(NEXT), .Q(STATE));  // open: Qn, preset, en, reset
  D_Flip_Flop #(.trigger("falling")) Q0 (.clk(CLK_out), .D(NEXT_2), .Q(STATE_2));  // open: Qn, preset, en, reset
  Clock CLK (.out(CLK_out));
  LED UP_Main (.in(comparator_1_gt));
  LED STOP_Main (.in(comparator_1_eq));
  Comparator #(.width(2), .mode("unsigned")) comparator_1 (
    .a({NEXT, NEXT_2}), .b({STATE, STATE_2}), .gt(comparator_1_gt), .eq(comparator_1_eq), .lt(comparator_1_lt));
  LED DOWN_Main (.in(comparator_1_lt));
  LED DOWN_Main_2 (.in(comparator_2_gt));
  Hex_Digit_Display hex_digit_display_1 (.value({in_3, STATE, STATE_2}));  // open: dp
  Hex_Digit_Display hex_digit_display_2 (.value({in_3, STATE, STATE_2}));  // open: dp
  Adder #(.width(4)) adder_1 (.a({in_3, STATE, STATE_2}), .b(in_6), .out(adder_1_out));  // open: cin, cout
  Hex_Digit_Display hex_digit_display_3 (.value({in_3, STATE, STATE_2}));  // open: dp
  Hex_Digit_Display hex_digit_display_4 (.value(adder_1_out));  // open: dp
  Hex_Digit_Display hex_digit_display_5 (.value(subtractor_1_out));  // open: dp
  Subtractor #(.width(4)) subtractor_1 (
    .a({in_3, STATE, STATE_2}), .b(in_4), .out(subtractor_1_out), .bin(comparator_2_eq));  // open: bout
  Comparator #(.width(4), .mode("unsigned")) comparator_2 (
    .a({in_3, STATE, STATE_2}), .b({in_5, F1_INPUT, F0_INPUT}), .gt(comparator_2_gt), .eq(comparator_2_eq),
    .lt(comparator_2_lt));
  Adder #(.width(4)) adder_2 (.a(adder_1_out), .b(in_6), .out(adder_2_out));  // open: cin, cout
  LED UP (.in(comparator_3_lt));
  Comparator #(.width(4), .mode("unsigned")) comparator_3 (
    .a(adder_1_out), .b({in_5, F1_INPUT, F0_INPUT}), .eq(comparator_3_eq), .lt(comparator_3_lt));  // open: gt
  LED STOP (.in(comparator_3_eq));
  LED DOWN (.in(comparator_4_gt));
  Comparator #(.width(4), .mode("unsigned")) comparator_4 (
    .a(subtractor_1_out), .b({in_5, F1_INPUT, F0_INPUT}), .gt(comparator_4_gt), .eq(comparator_4_eq));  // open: lt
  LED STOP_2 (.in(comparator_4_eq));
  LED UP_Main_2 (.in(comparator_2_lt));
  Hex_Digit_Display hex_digit_display_6 (.value(adder_2_out));  // open: dp
  LED STOP_Main_2 (.in(comparator_2_eq));
  LED UP_2 (.in(comparator_6_lt));
  LED STOP_3 (.in(comparator_6_eq));
  Hex_Digit_Display hex_digit_display_7 (.value(subtractor_2_out));  // open: dp
  Subtractor #(.width(4)) subtractor_2 (.a(subtractor_1_out), .b(in_4), .out(subtractor_2_out));  // open: bin, bout
  Comparator #(.width(4), .mode("unsigned")) comparator_5 (
    .a(subtractor_2_out), .b({in_5, F1_INPUT, F0_INPUT}), .gt(comparator_5_gt), .eq(comparator_5_eq));  // open: lt
  Adder #(.width(4)) adder_3 (.a(adder_2_out), .b(in_6), .out(adder_3_out));  // open: cin, cout
  Comparator #(.width(4), .mode("unsigned")) comparator_6 (
    .a(adder_2_out), .b({in_5, F1_INPUT, F0_INPUT}), .eq(comparator_6_eq), .lt(comparator_6_lt));  // open: gt
  LED DOWN_2 (.in(comparator_5_gt));
  LED STOP_4 (.in(comparator_5_eq));
  Hex_Digit_Display hex_digit_display_8 (.value(adder_3_out));  // open: dp
  Hex_Digit_Display hex_digit_display_9 (.value(subtractor_3_out));  // open: dp
  Subtractor #(.width(4)) subtractor_3 (.a(subtractor_2_out), .b(in_4), .out(subtractor_3_out));  // open: bin, bout

  // Notes on the sheet:
  //   ELEVATOR INPUT
  //    INTELLIGENT ELEVATOR CIRCUIT 
  //   Main Comparator
  //   Follow the Main circuit then Follow the First led on
  //   Main comparator to enter specific circuit
  //   UP FLOOR
  //   DOWN FLOOR
endmodule
