// Logisim project No.people circuits.circ as structural Verilog: 1 circuit, main circuit main
module main (
  input  [2:0] in_1
);

  wire decoder_1_out1, decoder_1_out2, decoder_1_out3, decoder_1_out4, decoder_1_out5, or_1_out;

  Decoder #(.select(3), .enable("false")) decoder_1 (
    .out1(decoder_1_out1), .out2(decoder_1_out2), .out3(decoder_1_out3), .out4(decoder_1_out4),
    .out5(decoder_1_out5), .sel(in_1));  // open: out0, out6, out7
  LED led_1 (.in(or_1_out));
  or or_1 (or_1_out, decoder_1_out1, decoder_1_out2, decoder_1_out3, decoder_1_out4, decoder_1_out5);
endmodule
