// Logisim project detect floor circuit.circ as structural Verilog: 1 circuit, main circuit main
module main (
  input  [1:0] in_1,
  input  [1:0] in_2,
  input  [1:0] in_3,
  input  [1:0] in_4,
  input  in_5,
  input  in_6,
  output [1:0] out_7,
  output out_8,
  output out_9,
  output out_10,
  output [1:0] out_11
);

  wire or_1_out;

  Comparator #(.width(1), .mode("unsigned")) comparator_1 (.a(in_5), .b(in_6), .gt(out_8), .eq(out_9), .lt(out_10));
  or or_1 (or_1_out, out_8, out_10);
  assign out_11 = {in_6, in_5} ^ out_7;  // XOR_Gate xor_1, 2 bits wide
  LED led_1 (.in(or_1_out));
  Multiplexer #(.select(2), .width(2), .enable("false")) multiplexer_1 (
    .in0(in_1), .in1(in_2), .in2(in_3), .in3(in_4), .out(out_7), .sel({out_10, out_8}));
  LED led_2 (.in(out_9));
endmodule
