// Logisim project first circuit.circ as structural Verilog: 1 circuit, main circuit main
module main (
  input  [3:0] in_1,
  input  in_2,
  input  in_3,
  input  in_4,
  output out_5,
  output out_6
);

  Hex_Digit_Display hex_digit_display_1 (.value(in_1), .dp(in_2));
  Hex_Digit_Display hex_digit_display_2 (.value(in_1));  // open: dp
  not not_1 (out_6, in_4);
  or or_1 (out_5, in_3, in_4);
endmodule
