// Logisim project floor.circ as structural Verilog: 1 circuit, main circuit main
module main (
  input  [1:0] in_1,
  input  [1:0] in_2,
  input  [1:0] in_3,
  input  [1:0] in_4,
  input  in_5,
  input  in_6,
  input  f1,
  input  f2,
  output [1:0] out_9
);

  wire and_1_out, clock_1_out, comparator_1_eq, comparator_1_gt, comparator_1_lt;
  wire [1:0] or_1_out;

  Comparator #(.width(1), .mode("unsigned")) comparator_1 (
    .a(in_5), .b(in_6), .gt(comparator_1_gt), .eq(comparator_1_eq), .lt(comparator_1_lt));
  and and_1 (and_1_out, in_6, comparator_1_eq);
  or or_1 (or_1_out[0], comparator_1_gt, and_1_out);
  or or_2 (or_1_out[1], and_1_out, comparator_1_lt);
  Clock clock_1 (.out(clock_1_out));
  Multiplexer #(.select(2), .width(2), .enable("false")) multiplexer_1 (
    .in0(in_1), .in1(in_2), .in2(in_3), .in3(in_4), .out(out_9), .sel(or_1_out));
  D_Flip_Flop d_ff_1 (.clk(clock_1_out));  // open: D, Q, Qn, preset, en, reset
  D_Flip_Flop d_ff_2 (.clk(clock_1_out));  // open: D, Q, Qn, preset, en, reset
  // AND_Gate and_2 is placed but not wired
  // AND_Gate and_3 is placed but not wired
  // AND_Gate and_4 is placed but not wired
endmodule
