// Logisim project test.circ as structural Verilog: 1 circuit, main circuit main
module main (
  input  [3:0] in_1,
  input  [3:0] in_2,
  input  in_3,
  input  in_4,
  input  in_5
);

  wire and_1_out, and_2_out, and_3_out, and_4_out, and_5_out, clock_1_out, comparator_1_eq, comparator_1_gt,
       comparator_1_lt, d_ff_1_q, d_ff_2_q, nand_1_out, nand_2_out, not_1_out, not_2_out, not_3_out,
       not_4_out, not_5_out, not_6_out, not_7_out, not_8_out, or_1_out, or_2_out, or_3_out, or_4_out,
       undriven;

  Comparator #(.width(4), .mode("unsigned")) comparator_1 (
    .a(in_1), .b(in_2), .gt(comparator_1_gt), .eq(comparator_1_eq), .lt(comparator_1_lt));
  not not_1 (not_1_out, comparator_1_gt);
  not not_2 (not_2_out, comparator_1_gt);
  not not_3 (not_3_out, comparator_1_lt);
  not not_4 (not_4_out, d_ff_2_q);
  not not_5 (not_5_out, undriven);
  nand nand_1 (nand_1_out, comparator_1_gt, undriven, d_ff_2_q);
  or or_1 (or_1_out, comparator_1_lt, comparator_1_eq, undriven, not_6_out);
  not not_6 (not_6_out, d_ff_2_q);
  or or_2 (or_2_out, comparator_1_eq, not_1_out, d_ff_2_q, not_5_out);
  nand nand_2 (nand_2_out, comparator_1_lt, not_2_out, undriven, d_ff_2_q);
  or or_3 (or_3_out, not_3_out, comparator_1_eq, undriven, not_4_out);
  or or_4 (or_4_out, comparator_1_eq, comparator_1_gt, not_5_out, d_ff_2_q);
  and and_1 (and_1_out, nand_2_out, or_3_out, or_4_out);
  Clock clock_1 (.out(clock_1_out));
  and and_2 (and_2_out, nand_1_out, or_1_out, or_2_out);
  D_Flip_Flop d_ff_1 (
    .clk(clock_1_out), .D(and_2_out), .Q(d_ff_1_q), .preset(in_5), .en(in_3), .reset(in_4));  // open: Qn
  D_Flip_Flop d_ff_2 (
    .clk(clock_1_out), .D(and_1_out), .Q(d_ff_2_q), .preset(in_5), .en(in_3), .reset(in_4));  // open: Qn
  not not_7 (not_7_out, d_ff_1_q);
  not not_8 (not_8_out, d_ff_2_q);
  and and_3 (and_3_out, d_ff_2_q, not_7_out);
  and and_4 (and_4_out, d_ff_1_q, not_8_out);
  LED led_1 (.in(and_3_out));
  and and_5 (and_5_out, d_ff_2_q, undriven);
  LED led_2 (.in(and_4_out));
  LED led_3 (.in(and_5_out));
endmodule
