// Logisim project SMALL CIRCUIT.circ as structural Verilog: 1 circuit, main circuit main
// A
module main (
  input  in_1
);

  wire A_q, A_qn, and_1_out, and_2_out, and_3_out, and_4_out, and_5_out, and_6_out, and_7_out, B_q, B_qn,
       C_q, C_qn, clock_1_out, or_1_out, or_2_out;
  wire [2:0] or_5_out;

  and and_1 (and_1_out, B_q, C_q);
  or or_1 (or_1_out, A_q, C_q);
  or or_2 (or_2_out, A_qn, B_qn);
  and and_2 (and_2_out, A_q, B_qn);
  and and_3 (and_3_out, B_q, C_q);
  and and_4 (and_4_out, B_qn, C_q);
  and and_5 (and_5_out, B_q, C_qn, A_qn);
  and and_6 (and_6_out, B_qn, C_qn);
  and and_7 (and_7_out, C_qn, A_qn);
  or or_3 (or_5_out[2], and_2_out, and_3_out);
  or or_4 (or_5_out[1], and_4_out, and_5_out);
  or or_5 (or_5_out[0], and_6_out, and_7_out);
  Clock clock_1 (.out(clock_1_out));
  Hex_Digit_Display hex_digit_display_1 (.value({in_1, or_5_out}));  // open: dp
  J_K_Flip_Flop A (.J(and_1_out), .clk(clock_1_out), .K(B_q), .Q(A_q), .Qn(A_qn));  // open: preset, en, reset
  J_K_Flip_Flop B (.J(C_q), .clk(clock_1_out), .K(or_1_out), .Q(B_q), .Qn(B_qn));  // open: preset, en, reset
  J_K_Flip_Flop C (.J(or_2_out), .K(1'b1), .Q(C_q), .Qn(C_qn));  // open: clk, preset, en, reset

  // Notes on the sheet:
  //   A
  //   B
  //   A bar
  //   C
  //   B BAR
  //   C BAR
  //   LOGIC SMALL CIRCUIT
  //   A+
  //   B+
  //   C+
  //   0 A+ B+ C+
endmodule
