// Logisim project xxx.circ as structural Verilog: 1 circuit, main circuit main
module main (
  input  in_1,
  input  in_2,
  input  in_3,
  input  [1:0] in_4,
  output out_5,
  output out_6
);

  wire multiplexer_1_out, not_1_out;

  Multiplexer #(.enable("false")) multiplexer_1 (.in0(in_1), .in1(in_2), .out(multiplexer_1_out), .sel(in_3));
  not not_1 (not_1_out, multiplexer_1_out);
  Multiplexer #(.select(2), .enable("false")) multiplexer_2 (
    .in0(not_1_out), .in1(not_1_out), .in2(not_1_out), .in3(not_1_out), .out(out_5), .sel(in_4));
  Multiplexer #(.select(2), .enable("false")) multiplexer_3 (
    .in0(multiplexer_1_out), .in1(multiplexer_1_out), .in2(multiplexer_1_out), .in3(multiplexer_1_out),
    .out(out_6), .sel(in_4));
endmodule
